# Fritzing sketch LolinD1Mini Shield (saved by Fritzing 0.9.3b)

parts:
  LCD2 = LCD screen
  R2 = Resistor [tolerance=±5% resistance=4.7k package=THT]
  DS2 = DS18B20 1-Wire Temperature Sensor [part_number=DS18B20]
  ENCODER3 = Rotary Encoder with switch (KY-040) [part_number=KY-040]
  U2 = 2-Channel 5v Relay Shield [package=relay-2ch5v10a]
  WeMos_D1_Mini_Protoboard_Shield1 = WeMos D1 Mini Protoboard Shield
  R4 = Resistor [tolerance=±5% resistance=10k package=THT]
  LCM1602_IIC2 = LCM1602 IIC [part_number="LCM1602 IIC" chip_label="LCM1602 IIC" package="DIP (Dual Inline) [THT]"]
  J4 = 3.81mm CamdenBoss Plug Socket - 3 [part_number=CTB93HE-3 package=THT]

nets:
  VSS: LCD2.VSS, LCM1602_IIC2.VSS
  VDD: LCD2.VDD, LCM1602_IIC2.VDD
  N1: LCD2.V0, LCM1602_IIC2.V0
  N2: LCD2.RS, LCM1602_IIC2.RS
  N3: LCD2.R/W, LCM1602_IIC2.RW
  N4: LCD2.E, LCM1602_IIC2.E
  N5: LCD2.DB0, LCM1602_IIC2.D0
  N6: LCD2.DB1, LCM1602_IIC2.D1
  N7: LCD2.DB2, LCM1602_IIC2.D2
  N8: LCD2.DB3, LCM1602_IIC2.D3
  N9: LCD2.DB4, LCM1602_IIC2.D4
  N10: LCD2.DB5, LCM1602_IIC2.D5
  N11: LCD2.DB6, LCM1602_IIC2.D6
  N12: LCD2.DB7, LCM1602_IIC2.D7
  N13: LCD2.LED+, LCM1602_IIC2.A
  N14: LCD2.LED-, LCM1602_IIC2.K
  N15: R2.Pin_0, WeMos_D1_Mini_Protoboard_Shield1.X3-Y8
  N16: R2.Pin_1, DS2.DQ, WeMos_D1_Mini_Protoboard_Shield1.D4, J4.pin1
  N17: ENCODER3.SW, WeMos_D1_Mini_Protoboard_Shield1.D6, WeMos_D1_Mini_Protoboard_Shield1.X2-Y5, WeMos_D1_Mini_Protoboard_Shield1.X3-Y5, R4.Pin_1
  N18: ENCODER3.DT, WeMos_D1_Mini_Protoboard_Shield1.D5
  N19: ENCODER3.CLK, WeMos_D1_Mini_Protoboard_Shield1.D0
  N20: U2.IN1, WeMos_D1_Mini_Protoboard_Shield1.D8
  N21: U2.IN2, WeMos_D1_Mini_Protoboard_Shield1.D7
  N22: WeMos_D1_Mini_Protoboard_Shield1.5V, WeMos_D1_Mini_Protoboard_Shield1.X3-Y10, WeMos_D1_Mini_Protoboard_Shield1.X4-Y8, WeMos_D1_Mini_Protoboard_Shield1.X5-Y8, WeMos_D1_Mini_Protoboard_Shield1.X6-Y8, WeMos_D1_Mini_Protoboard_Shield1.X7-Y8, R4.Pin_0
  N23: WeMos_D1_Mini_Protoboard_Shield1.D1, LCM1602_IIC2.SDA
  N24: WeMos_D1_Mini_Protoboard_Shield1.D2, LCM1602_IIC2.SCL
  N25: WeMos_D1_Mini_Protoboard_Shield1.X4-Y7, WeMos_D1_Mini_Protoboard_Shield1.X5-Y7, WeMos_D1_Mini_Protoboard_Shield1.X6-Y7, WeMos_D1_Mini_Protoboard_Shield1.X7-Y7

notes:
  Sainsmart IIC/I2C/TWI 1602 Serial LCD or 2004 Serial LCD
  DS18B20 Temp Sensor
  KY-040 Rotary Encoder
  SunFounder 2 Channel 5V Relay
  10K 1/4 W 5% Resistor for KY-040 SW Pin for hardware debouncing
  4.7k 1/2 Watt 5% Resistor for Temprature data
  Power and ground omitted for clarity

custom parts:
  Rotary Encoder with switch (KY-040): A Rotary Encoder with switch
  2-Channel 5v Relay Shield: 2 Channel 5v Relay Shield w. 2x SPD-06VDC-SD-C
  LCM1602 IIC: I2C-Module to use a 1602 or 2004 LCD on with the wire.h libory Serial LCD Modul
  3.81mm CamdenBoss Plug Socket - 3: CamdenBoss CTB93HE-3 3.81mm (0.15") Pitch Standard Profile 90 ̊ Rising Clamp Terminal, 4 pole The real-life connectors are modular, made up of two or three connector blocks slotted together. These can be further slotted together to make larger connectors. Fritzing part is derived from Screw terminals by Lionel Michel. Because of the offset between connection pins and screw terminals, these are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
